// Digital circuit CPU.dig as structural Verilog
module CPU (
  input  Rise,
  input  Fall,
  input  [7:0] ROM,
  input  [7:0] MemIn,
  output [7:0] ROMAddr,
  output [7:0] MemAddr,
  output MemWrite,
  output [7:0] MemOut
);

  wire alu_1_cout, and_1_out, and_2_out, carry, control_1_nextfetchmode, destMemAddr, destRa, not_2_out,
       setImmed, setRegs;
  wire [0:0] control_1_pcmode, control_1_pcmode_2;
  wire [1:0] control_1_dest, control_1_srca, control_1_srcb;
  wire [3:0] Active_registers_q, control_1_alumode;
  wire [7:0] GPRs_da, GPRs_db, Immediate_value_q, multiplexer_1_out, multiplexer_2_out, multiplexer_3_out,
       PC_Adder_s;

  Control control_1 (
    .Rise(Rise), .Instruction(ROM[7:4]), .NextFetchMode(control_1_nextfetchmode),
    .PCMode({control_1_pcmode_2[0], control_1_pcmode[0]}), .ALUMode(control_1_alumode),
    .SrcA(control_1_srca), .SrcB(control_1_srcb), .Dest(control_1_dest));
  Register #(.Bits(8)) Immediate_value (.D(ROM), .C(Rise), .en(setImmed), .Q(Immediate_value_q));
  Register #(.Bits(4)) Active_registers (.D(ROM[3:0]), .C(Rise), .en(setRegs), .Q(Active_registers_q));
  Decoder #(.Selector_Bits(2)) decoder_1 (
    .sel(control_1_dest), .out_0(MemWrite), .out_1(destMemAddr), .out_2(destRa));  // open: out_3
  // Probe Active rA on Active_registers_q[3:2]
  // Probe Active rB on Active_registers_q[1:0]
  RegisterFile #(.Bits(8)) GPRs (
    .Din(MemOut), .we(destRa), .Rw(Active_registers_q[3:2]), .C(Fall), .Ra(Active_registers_q[3:2]),
    .Rb(Active_registers_q[1:0]), .Da(GPRs_da), .Db(GPRs_db));
  Register #(.Bits(8), .isProgramCounter("true")) PC (.D(multiplexer_3_out), .C(Fall), .en(1'b1), .Q(ROMAddr));
  Multiplexer #(.Selector_Bits(2), .Bits(8)) multiplexer_1 (
    .sel(control_1_srca), .in_0(MemIn), .in_1(Immediate_value_q), .in_2(GPRs_da), .in_3(GPRs_db),
    .out(multiplexer_1_out));
  Multiplexer #(.Selector_Bits(2), .Bits(8)) multiplexer_2 (
    .sel(control_1_srcb), .in_0(MemIn), .in_1(Immediate_value_q), .in_2(GPRs_da), .in_3(GPRs_db),
    .out(multiplexer_2_out));
  ALU alu_1 (
    .Mode(control_1_alumode), .A(multiplexer_1_out), .B(multiplexer_2_out), .Cin(carry), .Cout(alu_1_cout),
    .Out(MemOut));  // open: Zero
  Register nextFetchMode (.D(control_1_nextfetchmode), .C(Fall), .en(1'b1), .Q(setImmed));
  and and_1 (and_1_out, control_1_pcmode[0], carry);
  not not_1 (setRegs, setImmed);
  not not_2 (not_2_out, control_1_pcmode_2[0]);
  Register u_Carry (.D(alu_1_cout), .C(Fall), .en(1'b1), .Q(carry));
  Register #(.Bits(8)) Memory_address (.D(MemOut), .C(Fall), .en(destMemAddr), .Q(MemAddr));
  and and_2 (and_2_out, control_1_pcmode[0], not_2_out);
  Add #(.Bits(8)) PC_Adder (
    .a(ROMAddr), .b({{7{1'b0}}, control_1_pcmode_2[0]}), .c_i(and_1_out), .s(PC_Adder_s));  // open: c_o
  Multiplexer #(.Bits(8)) multiplexer_3 (.sel(and_2_out), .in_0(PC_Adder_s), .in_1(MemOut), .out(multiplexer_3_out));

  // Other names for the same wires on the sheet: destMem = MemWrite; pc[7:0] = ROMAddr

  // Notes on the sheet:
  //   Rise > ready > fall
  //   Instruction decode
  //   Ready ASAP
  //   Data fetch
  //   Execute
  //   Fall > ready > next rise
  //   Fetch next instruction
  //   Write back
  //   <-- This PC thing has grown to a pile of mess
endmodule
