// Digital circuit Main.dig as structural Verilog
module Main (
  input  Clock,
  input  Enable_clock
);

  wire and_1_out, cpu_1_memwrite, fall, Manual_pulse_out, or_1_out, rise;
  wire [7:0] cpu_1_memaddr, cpu_1_memout, cpu_1_romaddr, ramdualport_1_d, rom_1_d;

  CPU cpu_1 (
    .Rise(rise), .Fall(fall), .ROM(rom_1_d), .MemIn(ramdualport_1_d), .ROMAddr(cpu_1_romaddr),
    .MemAddr(cpu_1_memaddr), .MemWrite(cpu_1_memwrite), .MemOut(cpu_1_memout));
  Button Manual_pulse (.out(Manual_pulse_out));
  and and_1 (and_1_out, Enable_clock, Clock);
  or or_1 (or_1_out, Manual_pulse_out, and_1_out);
  RisingEdgeDetector risingedgedetector_1 (.In(or_1_out), .Out(rise));
  FallingEdgeDetector fallingedgedetector_1 (.In(or_1_out), .Out(fall));
  // Probe Cycle on or_1_out
  ROM #(.AddrBits(8), .Bits(8)) rom_1 (.A(cpu_1_romaddr), .sel(1'b1), .D(rom_1_d));
  RAMDualPort #(.AddrBits(8), .Bits(8)) ramdualport_1 (
    .A(cpu_1_memaddr), .Din(cpu_1_memout), .str(cpu_1_memwrite), .C(fall), .ld(1'b1), .D(ramdualport_1_d));

  // Notes on the sheet:
  //   Clock: Hz: 100
  //   contents of rom_1 (hex, n*v repeats v):
  //   10,ff,14,1,1c,6,61,e0,dc,51,1c,c,51,e0,dc
endmodule
